# Fritzing sketch schema (saved by Fritzing 0.9.3b)

parts:
  U1 = LuaNode32 / ESP32
  U2 = 2.4" TFT LCD screen, SPI, Touch-enabled
  Součástka1 = Adafruit SHT31-D Sensirion Temperature/Humidity Sensor [part_number="Adafruit #2857"]
  HLK-PM1 = HLK-PM01
  KY-1 = Keyes Relay [package=THT]
  Q1 = Basic FET N-Channel [package="DPak [SMD]"]
  S1 = Pushbutton [package="[SMD]"]

nets:
  GND: U1.EN, U1.GND, U2.RESET, U2.GND, Součástka1.GND, HLK-PM1.-Vo, KY-1.ground, Q1.source, S1.Pin_1, S1.Pin_2
  VIN: U1.Vin, U2.LED, U2.VCC, HLK-PM1.+Vo, KY-1.power
  3V3: U1.3V3, Součástka1.VIN
  N1: U1.D15, U2.CS
  N2: U1.D2, U2.DC
  N3: U1.D4, U2.T_CS
  N4: U1.RX2, Q1.Gate
  N5: U1.D18, U2.T_CLK, U2.SCL
  N6: U1.D19, U2.T_DO, U2.SDO
  N7: U1.D21, Součástka1.SDA
  N8: U1.D22, Součástka1.SCL
  N9: U1.D23, U2.T_DIN, U2.SDA
  N10: KY-1.signal, Q1.drain

notes:
  ILI9341 to ESP32:
  T_IRQ not connected
  T_DO to 19 (MISO)
  T_DIN to 23 (MOSI)
  T_CS to 4
  T_CLK to 18 (SCLK)
  SDO (MISO) to 19
  LED to 5V (or 3.3V)
  SCK to 18
  SDI (MOSI) to 23
  DC to 2
  RESET to EN (reset)
  CS to 15
  GND to GND
  VCC to 5V (or 3.3V)
  Reset
  220V
  Normaly open relay switch to turn off/on boiler

custom parts:
  LuaNode32 / ESP32: ESP32 based LuaNode32
  2.4" TFT LCD screen, SPI, Touch-enabled: 2.4", ILI9341-based TFT LCD screen with touch-sensing using the XPT2046 controller, SPI-compatible. There is also an SD-card version that is non-touch enabled but uses exactly the same board and pinout. This part is for both, though it should be noted that the SD reader and the touch screen are mutually incompatible
  Adafruit SHT31-D Sensirion Temperature/Humidity Sensor: Sensirion Temperature/Humidity sensors are some of the finest & highest-accuracy devices you can get. And, finally we have some that have a true I2C interface for easy reading. The SHT31-D sensor has an excellent ±2% relative humidity and ±0.3°C accuracy for most uses. Unlike earlier SHT sensors, this sensor has a true I2C interface, and (bonus!) even with two address options. It also is 3V or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
  Keyes Relay: The Keyes 5V relay module is suitable for SCM development, home appliance control. It uses a 5V~12V TIL control signal which can control DC / AC signal.
